# Fritzing sketch flight_controller (saved by Fritzing 0.9.3b)

parts:
  Часть1 = Arduino Nano (Rev3.0) (ICSP)
  Часть2 = MicroSD Card Module
  GY2 = MPU-6050 Board GY-521 [form="♀ (female)" package=THT]
  GSM_SIM_GPSR_SMS_SIM900_SIM1 = SIM800L [package=THT]
  GY-NEO6MV3 = SUP500F [package=sup500f]
  R1 = Resistor [tolerance=±5% resistance=220 package=THT]
  R2 = Resistor [tolerance=±5% resistance=220 package="2010 [SMD]"]
  Part1 = KY-012 Active Buzzer Module [package="Breakout board"]
  S1 = Pushbutton [package="[SMD]"]
  VCC2 = Battery block 9V

nets:
  N1: Часть1.D1/TX, GY-NEO6MV3.VCC
  N2: Часть1.D0/RX, R1.Pin_1
  N3: Часть1.D5, Часть2.CS
  GND: Часть1.D7, Часть1.GND, Часть2.GND, GY2.pin2, Part1.-, S1.Pin_1, S1.Pin_2
  N4: Часть1.D9, GSM_SIM_GPSR_SMS_SIM900_SIM1.SIM_TXD
  N5: Часть1.D10, GSM_SIM_GPSR_SMS_SIM900_SIM1.SIM_RXD
  N6: Часть1.D11/MOSI, Часть2.MOSI
  N7: Часть1.D12/MISO, Часть2.SCK
  5V: Часть1.5V, Часть2.VCC, GY2.pin1, GY-NEO6MV3.TX-O, Part1.S, S1.Pin_3, S1.Pin_4
  N8: Часть1.A5, GY2.pin3
  N9: Часть1.A4, GY2.pin4
  N10: Часть1.D13/SCK, Часть2.MISO
  N11: GY-NEO6MV3.RX-I, R2.Pin_1, VCC2.-
  N12: GY-NEO6MV3.GND, R1.Pin_0, R2.Pin_0

notes:
  GND: Black
  VCC: Red
  RX: Yellow
  TX: Green
  4.7kOhm
  10kOhm

custom parts:
  MPU-6050 Board GY-521: Acelerometro y Giroscopio MPU-6050 Board GY-521
  KY-012 Active Buzzer Module: Active Piezoelectric Buzzer Module Keyes KY-012, it produces single-tone sound when signal is high.
