# Fritzing sketch scale (saved by Fritzing 0.9.3b)

parts:
  Часть1 = Arduino Uno (Rev3)  # not connected
  LCD1 = LCD screen
  Часть2 = HX711 Weighing Sensor Module
  Часть4 = Memoire 1.0 - SD card log shield
  U1 = POT [package=pot_alpha_rv16af-20]
  S1 = Momentary Switch [package=ksa_sealed_tac_switch]

nets:
  N1: LCD1.V0, U1.S
  N2: LCD1.RS, Часть4.DIG_9
  N3: LCD1.E, Часть4.DIG_8
  N4: LCD1.DB4, Часть4.DIG_5
  N5: LCD1.DB5, Часть4.DIG_4
  N6: LCD1.DB6, Часть4.DIG_3
  N7: LCD1.DB7, Часть4.DIG_2
  N8: LCD1.LED+, Часть4.+5V
  N9: LCD1.LED-, Часть4.GND
  N10: Часть2.DO/RX, Часть4.A_IN_1
  N11: Часть2.CK/TX, Часть4.A_IN_0
  N12: Часть4.DIG_6, S1.2
