# Fritzing sketch transmitter (saved by Fritzing 0.9.3b)

parts:
  Часть1 = Arduino Nano (Rev3.0) (ICSP)
  Часть2 = NRF24L01+ Breakout Board
  VCC1 = Battery block 9V
  LED1 = LEDs [package=led10mm]
  LED2 = LEDs [package=led10mm]
  S3 = Pushbutton [package=THT]  # not connected
  S4 = Pushbutton [package="[SMD]"]

nets:
  GND: Часть1.D4, Часть1.GND, Часть2.GND, VCC1.-, S4.Pin_1, S4.Pin_2
  N1: Часть1.D5, LED1.C
  N2: Часть1.D6, LED2.C
  N3: Часть1.D9, Часть2.CE
  N4: Часть1.D10, Часть2.CS
  N5: Часть1.D11/MOSI, Часть2.MOSI
  N6: Часть1.D12/MISO, Часть2.MISO
  5V: Часть1.5V, Часть2.VCC
  N7: Часть1.D13/SCK, Часть2.SCK
